# Fritzing sketch atari-600xl-pbi-nolevel-0p1 (saved by Fritzing 0.9.9b)
circuit board: 10.6364cm x 7.66447cm
breadboards: 1

parts:
  R1 = Resistor [tolerance=±5% resistance=10k power=0.25 package=THT]
  R3 = Resistor [tolerance=±5% resistance=220 power=0.25 package=THT]
  LEVELSHT-3 = Adafruit 4-channel I2C-safe Bi-directional Logic Level Converter [part_number="Adafruit #757"]
  R2 = Resistor [tolerance=±5% power=0.25 resistance=10k package=THT]
  MIC = Breakout Board for Electret Microphone
  LEVELSHT-2 = Adafruit 4-channel I2C-safe Bi-directional Logic Level Converter [part_number="Adafruit #757"]
  LEVELSHT-1 = Adafruit 4-channel I2C-safe Bi-directional Logic Level Converter [part_number="Adafruit #757"]
  J1 = shrouded pin header, 50 pins [form="♂ (shrouded male)"]
  R4 = Resistor [tolerance=±5% resistance=0 power=0.25 package=THT]
  R5 = Resistor [tolerance=±5% resistance=0 power=0.25 package=THT]
  U1 = ESP32-38PinWide [part_number=ESP32-38Pin]
  J2-TFT-DISPLAY = female pin header, 8 pins [form="♀ (female)"]
  J3-SDCARD = female pin header, 6 pins [form="♀ (female)"]

nets (from the pcb view):
  N1: R1.Pin_0, J1.pin34
  N2: R1.Pin_1, R2.Pin_0, R4.Pin_1, U1.EN
  N3: R3.Pin_0, MIC.AUD
  N4: R3.Pin_1, U1.GPIO2, J2-TFT-DISPLAY.pin3
  GND: LEVELSHT-3.GND, R2.Pin_1, MIC.GND, J1.pin1, J1.pin10, J1.pin15, J1.pin35, J1.pin36, U1.GND, J2-TFT-DISPLAY.pin2, J3-SDCARD.pin6
  N5: LEVELSHT-3.A4, U1.GPIO27
  N6: LEVELSHT-3.A3, U1.GPIO14
  N7: LEVELSHT-3.A2, U1.GPIO12
  N8: LEVELSHT-3.A1, U1.GPIO13
  N9: LEVELSHT-3.LV, MIC.VCC, LEVELSHT-2.LV, R5.Pin_1, U1.3.3
  N10: LEVELSHT-3.B4, J1.pin11
  N11: LEVELSHT-3.B3, J1.pin12
  N12: LEVELSHT-3.B2, J1.pin13
  N13: LEVELSHT-3.B1, J1.pin14
  N14: LEVELSHT-3.HV, LEVELSHT-2.HV, LEVELSHT-1.LV, LEVELSHT-1.HV, J1.pin24, J1.pin27, U1.VIN
  GND_2: LEVELSHT-2.GND, LEVELSHT-1.GND, J1.pin26, J1.pin30
  N15: LEVELSHT-2.A4, U1.GPIO3
  N16: LEVELSHT-2.A3, U1.GPIO1
  N17: LEVELSHT-2.A2, U1.GPIO22
  N18: LEVELSHT-2.A1, U1.GPIO23
  N19: LEVELSHT-2.B4, J1.pin40
  N20: LEVELSHT-2.B3, J1.pin39
  N21: LEVELSHT-2.B2, J1.pin38
  N22: LEVELSHT-2.B1, J1.pin37
  N23: LEVELSHT-1.A4, U1.GPIO15, J2-TFT-DISPLAY.pin5, J3-SDCARD.pin1
  N24: LEVELSHT-1.A3, U1.GPIO8, J3-SDCARD.pin4
  N25: LEVELSHT-1.A2, U1.GPIO6, J2-TFT-DISPLAY.pin7, J3-SDCARD.pin2
  N26: LEVELSHT-1.A1, U1.GPIO7, J2-TFT-DISPLAY.pin6, J3-SDCARD.pin3
  N27: LEVELSHT-1.B4, J1.pin33
  N28: LEVELSHT-1.B3, J1.pin50
  N29: LEVELSHT-1.B2, J1.pin22
  N30: LEVELSHT-1.B1, J1.pin18
  N31: J1.pin2, U1.GPIO36
  N32: J1.pin3, U1.GPIO39
  N33: J1.pin4, U1.GPIO34
  N34: J1.pin5, U1.GPIO35
  N35: J1.pin6, U1.GPIO32
  N36: J1.pin7, U1.GPIO33
  N37: J1.pin8, U1.GPIO25
  N38: J1.pin9, U1.GPIO26
  N39: J1.pin16, U1.GPIO9
  N40: J1.pin28, U1.GPIO10
  N41: J1.pin31, U1.GPIO11
  N42: J1.pin41, U1.GPIO21
  N43: J1.pin42, U1.GPIO19
  N44: J1.pin43, U1.GPIO18
  N45: J1.pin44, U1.GPIO5
  N46: J1.pin45, U1.GPIO17
  N47: J1.pin47, U1.GPIO16
  N48: J1.pin48, U1.GPIO4
  N49: J1.pin49, U1.GPIO0
  N50: R4.Pin_0, J2-TFT-DISPLAY.pin4
  N51: R5.Pin_0, J2-TFT-DISPLAY.pin1, J2-TFT-DISPLAY.pin8, J3-SDCARD.pin5

notes:
  1) https://www.amazon.com/Connector-40p-98-Finger-Through-Durable/dp/B09MZXJ8Q3/ref=sr_1_15?crid=XJIJ1S8Y0NPS&keywords=edge%2Bconnector%2B0.1%2Binches&qid=1644340803&sprefix=edge%2Bconnector%2B0.1%2Binches%2Caps%2C406&sr=8-15&th=1
  2) https://www.amazon.com/HiLetgo-ESP-WROOM-32-Development-Microcontroller-Integrated/dp/B0718T232Z/ref=sr_1_10?keywords=ESP32+38+pin&qid=1644360022&sr=8-10
  3) https://www.amazon.com/KeeYees-Channels-Converter-Bi-Directional-Shifter/dp/B07LG646VS/ref=sr_1_3?keywords=4-channel+I2C-safe+Bi-directional+Logic+Level+Converter+-+BSS138&qid=1644509232&sr=8-3
  unused pins

custom parts:
  Adafruit 4-channel I2C-safe Bi-directional Logic Level Converter: Because the Arduino (and Basic Stamp) are 5V devices, and most modern sensors, displays, flash cards and modes are 3.3V-only, many makers find that they need to perform level shifting/conversion to protect the 3.3V device from 5V. We do have some other handy level shifters in the shop, from the DIP 74LVC245 to the fancy bi-directional TXB0108. However, neither of these are happy to work with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
  ESP32-38PinWide: Generic 38-Pin ESP32 with wide format (only access to one side of pins on a breadboard) based on Stephen Lilley's HiLetgo ESP-WROOM-32 ESP32 ESP-32S Development Board.
