# Fritzing sketch atari-600xl-pbi-nolevel-0p2 (saved by Fritzing 0.9.9b)
circuit board: 10.6364cm x 7.66447cm
breadboards: 1

parts:
  R1 = Resistor [tolerance=±5% resistance=10k power=0.25 package=THT]
  R3 = Resistor [tolerance=±5% resistance=220 power=0.25 package=THT]
  LEVELSHT-3 = Adafruit 4-channel I2C-safe Bi-directional Logic Level Converter [part_number="Adafruit #757"]
  R2 = Resistor [tolerance=±5% power=0.25 resistance=10k package=THT]
  MIC = Breakout Board for Electret Microphone
  LEVELSHT-2 = Adafruit 4-channel I2C-safe Bi-directional Logic Level Converter [part_number="Adafruit #757"]
  LEVELSHT-1 = Adafruit 4-channel I2C-safe Bi-directional Logic Level Converter [part_number="Adafruit #757"]
  R4 = Resistor [tolerance=±5% resistance=0 power=0.25 package=THT]
  R5 = Resistor [tolerance=±5% resistance=0 power=0.25 package=THT]
  U1 = ESP32-38PinWide [part_number=ESP32-38Pin]
  J2-TFT-DISPLAY = female pin header, 8 pins [form="♀ (female)"]
  J3-SDCARD = female pin header, 6 pins [form="♀ (female)"]
  J2 = female pin header, 25 pins [form="♀ (female)"]
  J3 = female pin header, 25 pins [form="♀ (female)"]
  J4 = female pin header, 3 pins [form="♀ (female)"]

nets:
  RST_O: R1.Pin_0, J3.pin9
  RST33: R1.Pin_1, R2.Pin_0, R4.Pin_1, U1.EN
  N1: R3.Pin_0, MIC.AUD
  DCRS/ESP_MIC: R3.Pin_1, U1.GPIO2, J2-TFT-DISPLAY.pin3
  GND: LEVELSHT-3.GND, R2.Pin_1, MIC.GND, LEVELSHT-2.GND, LEVELSHT-1.GND, U1.GND, J2-TFT-DISPLAY.pin2, J3-SDCARD.pin6, J2.pin11, J2.pin16, J2.pin25, J3.pin1, J3.pin5, J3.pin10, J3.pin11, J4.pin1, J4.pin2, J4.pin3
  ESP_D0: LEVELSHT-3.A4, U1.GPIO27
  ESP_D2: LEVELSHT-3.A3, U1.GPIO14
  ESP_D4: LEVELSHT-3.A2, U1.GPIO12
  ESP_D6: LEVELSHT-3.A1, U1.GPIO13
  3.3V: LEVELSHT-3.LV, MIC.VCC, LEVELSHT-2.LV, LEVELSHT-1.LV, R5.Pin_1, U1.3.3
  D0_IO: LEVELSHT-3.B4, J2.pin15
  D2_IO: LEVELSHT-3.B3, J2.pin14
  D4_IO: LEVELSHT-3.B2, J2.pin13
  D6_IO: LEVELSHT-3.B1, J2.pin12
  5V: LEVELSHT-3.HV, LEVELSHT-2.HV, LEVELSHT-1.HV, U1.VIN, J2.pin2, J3.pin2
  ESP_D1: LEVELSHT-2.A4, U1.GPIO3
  ESP_D3: LEVELSHT-2.A3, U1.GPIO1
  ESP_D5: LEVELSHT-2.A2, U1.GPIO22
  ESP_D7: LEVELSHT-2.A1, U1.GPIO23
  D1_IO: LEVELSHT-2.B4, J3.pin15
  D3_IO: LEVELSHT-2.B3, J3.pin14
  D5_IO: LEVELSHT-2.B2, J3.pin13
  D7_IO: LEVELSHT-2.B1, J3.pin12
  CS/ESP_RDY: LEVELSHT-1.A4, U1.GPIO15, J2-TFT-DISPLAY.pin5, J3-SDCARD.pin1
  ESP_ES/MISO: LEVELSHT-1.A3, U1.GPIO8, J3-SDCARD.pin4
  ESP_MPD/SCLK: LEVELSHT-1.A2, U1.GPIO6, J2-TFT-DISPLAY.pin7, J3-SDCARD.pin2
  ESP_IRQ/MOSI: LEVELSHT-1.A1, U1.GPIO7, J2-TFT-DISPLAY.pin6, J3-SDCARD.pin3
  RDY_I: LEVELSHT-1.B4, J3.pin8
  ES_I: LEVELSHT-1.B3, J3.pin25
  MPD_I: LEVELSHT-1.B2, J2.pin4
  IRQ_I: LEVELSHT-1.B1, J2.pin8
  N2: R4.Pin_0, J2-TFT-DISPLAY.pin4
  N3: R5.Pin_0, J2-TFT-DISPLAY.pin1, J2-TFT-DISPLAY.pin8, J3-SDCARD.pin5
  A0_O: U1.GPIO36, J2.pin24
  A2_0: U1.GPIO39, J2.pin23
  A4_O: U1.GPIO34, J2.pin22
  A6_O: U1.GPIO35, J2.pin21
  A7_O: U1.GPIO32, J2.pin20
  A9_O: U1.GPIO33, J2.pin19
  A11_O: U1.GPIO25, J2.pin18
  A13_O: U1.GPIO26, J2.pin17
  PH2_O: U1.GPIO9, J2.pin10
  RW_O: U1.GPIO10, J3.pin3
  REF_O: U1.GPIO11, J3.pin6
  A1_O: U1.GPIO0, J3.pin24
  A3_O: U1.GPIO4, J3.pin23
  A5_O: U1.GPIO16, J3.pin22
  A8_O: U1.GPIO17, J3.pin20
  A10_O: U1.GPIO5, J3.pin19
  A12_O: U1.GPIO18, J3.pin18
  A14_O: U1.GPIO19, J3.pin17
  A15_O: U1.GPIO21, J3.pin16

notes:
  1) https://www.amazon.com/Connector-40p-98-Finger-Through-Durable/dp/B09MZXJ8Q3/ref=sr_1_15?crid=XJIJ1S8Y0NPS&keywords=edge%2Bconnector%2B0.1%2Binches&qid=1644340803&sprefix=edge%2Bconnector%2B0.1%2Binches%2Caps%2C406&sr=8-15&th=1
  2) https://www.amazon.com/HiLetgo-ESP-WROOM-32-Development-Microcontroller-Integrated/dp/B0718T232Z/ref=sr_1_10?keywords=ESP32+38+pin&qid=1644360022&sr=8-10
  3) https://www.amazon.com/KeeYees-Channels-Converter-Bi-Directional-Shifter/dp/B07LG646VS/ref=sr_1_3?keywords=4-channel+I2C-safe+Bi-directional+Logic+Level+Converter+-+BSS138&qid=1644509232&sr=8-3
  unused pins

custom parts:
  Adafruit 4-channel I2C-safe Bi-directional Logic Level Converter: Because the Arduino (and Basic Stamp) are 5V devices, and most modern sensors, displays, flash cards and modes are 3.3V-only, many makers find that they need to perform level shifting/conversion to protect the 3.3V device from 5V. We do have some other handy level shifters in the shop, from the DIP 74LVC245 to the fancy bi-directional TXB0108. However, neither of these are happy to work with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
  ESP32-38PinWide: Generic 38-Pin ESP32 with wide format (only access to one side of pins on a breadboard) based on Stephen Lilley's HiLetgo ESP-WROOM-32 ESP32 ESP-32S Development Board.
