# Fritzing sketch atari-600xl-pbi-nolevel (saved by Fritzing 0.9.9b)
circuit board: 10.3869cm x 7.32109cm
breadboards: 1

parts:
  R1 = Resistor [tolerance=±5% resistance=10k power=0.25 package=THT]
  R3 = Resistor [tolerance=±5% resistance=220 power=0.25 package=THT]
  LEVELSHT-3 = Adafruit 4-channel I2C-safe Bi-directional Logic Level Converter [part_number="Adafruit #757"]
  R2 = Resistor [tolerance=±5% power=0.25 resistance=10k package=THT]
  MIC = Breakout Board for Electret Microphone
  LEVELSHT-2 = Adafruit 4-channel I2C-safe Bi-directional Logic Level Converter [part_number="Adafruit #757"]
  LEVELSHT-1 = Adafruit 4-channel I2C-safe Bi-directional Logic Level Converter [part_number="Adafruit #757"]
  J1 = shrouded pin header, 50 pins [form="♂ (shrouded male)"]
  J2-TFT-DISPLAY = female pin header, 8 pins [form="♀ (female)"]
  R4 = Resistor [tolerance=±5% resistance=0 power=0.25 package=THT]
  R5 = Resistor [tolerance=±5% resistance=0 power=0.25 package=THT]
  J3-SDCARD = female pin header, 6 pins [form="♀ (female)"]
  U1 = ESP32-38PinWide [part_number=ESP32-38Pin]

nets:
  RST_O: R1.Pin_0, J1.pin42
  RST33: R1.Pin_1, R2.Pin_0, R4.Pin_1, U1.EN
  N1: R3.Pin_0, MIC.AUD
  DCRS/ESP_MIC: R3.Pin_1, J2-TFT-DISPLAY.pin3, U1.GPIO2
  GND: LEVELSHT-3.GND, R2.Pin_1, MIC.GND, LEVELSHT-2.GND, LEVELSHT-1.GND, J1.pin11, J1.pin40, J1.pin41, J1.pin46, J1.pin50, J2-TFT-DISPLAY.pin2, J3-SDCARD.pin6, U1.GND
  ESP_D6: LEVELSHT-3.A4, U1.GPIO35
  ESP_D4: LEVELSHT-3.A3, U1.GPIO32
  ESP_D2: LEVELSHT-3.A2, U1.GPIO33
  ESP_D0: LEVELSHT-3.A1, U1.GPIO25
  3.3V: LEVELSHT-3.LV, MIC.VCC, LEVELSHT-2.LV, LEVELSHT-1.LV, R5.Pin_1, U1.3.3
  D6_IO: LEVELSHT-3.B4, J1.pin12
  D4_IO: LEVELSHT-3.B3, J1.pin13
  D2_IO: LEVELSHT-3.B2, J1.pin14
  D0_IO: LEVELSHT-3.B1, J1.pin15
  5V: LEVELSHT-3.HV, LEVELSHT-2.HV, LEVELSHT-1.HV, J1.pin2, J1.pin49, U1.VIN
  ESP_D1: LEVELSHT-2.A4, U1.GPIO23
  ESP_D3: LEVELSHT-2.A3, U1.GPIO22
  ESP_D5: LEVELSHT-2.A2, U1.GPIO1
  ESP_D7: LEVELSHT-2.A1, U1.GPIO3
  D1_IO: LEVELSHT-2.B4, J1.pin36
  D3_IO: LEVELSHT-2.B3, J1.pin37
  D5_IO: LEVELSHT-2.B2, J1.pin38
  D7_IO: LEVELSHT-2.B1, J1.pin39
  CS/ESP_RDY: LEVELSHT-1.A4, J2-TFT-DISPLAY.pin5, J3-SDCARD.pin1, U1.GPIO15
  ESP_ES/MISO: LEVELSHT-1.A3, J3-SDCARD.pin4, U1.GPIO8
  ESP_IRQ/MOSI: LEVELSHT-1.A2, J2-TFT-DISPLAY.pin6, J3-SDCARD.pin3, U1.GPIO7
  ESP_MPD/SCLK: LEVELSHT-1.A1, J2-TFT-DISPLAY.pin7, J3-SDCARD.pin2, U1.GPIO6
  RDY_I: LEVELSHT-1.B4, J1.pin43
  ES_I: LEVELSHT-1.B3, J1.pin26
  IRQ_I: LEVELSHT-1.B2, J1.pin8
  MPD_I: LEVELSHT-1.B1, J1.pin4
  AUD_I: J1.pin1
  CAS_O: J1.pin5
  NOT CONNECTED 2: J1.pin6
  NOT CONNECTED 3: J1.pin7
  NOT CONNECTED 1: J1.pin9
  PH2_O: J1.pin10, U1.GPIO36
  A13_O: J1.pin17, U1.GPIO26
  A11_O: J1.pin18, U1.GPIO27
  A9_O: J1.pin19, U1.GPIO14
  A7_O: J1.pin20, U1.GPIO12
  A6_O: J1.pin21, U1.GPIO13
  A4_O: J1.pin22, U1.GPIO9
  A2_0: J1.pin23, U1.GPIO10
  A0_O: J1.pin24, U1.GPIO11
  A1_O: J1.pin27, U1.GPIO21
  A3_O: J1.pin28, U1.GPIO19
  A5_O: J1.pin29, U1.GPIO18
  A8_O: J1.pin31, U1.GPIO5
  A10_O: J1.pin32, U1.GPIO17
  A12_O: J1.pin33, U1.GPIO16
  A14_O: J1.pin34, U1.GPIO4
  A15_O: J1.pin35, U1.GPIO0
  CASINH_O: J1.pin44
  REF_O: J1.pin45, U1.GPIO34
  RAS_O: J1.pin47
  RW_O: J1.pin48, U1.GPIO39
  N2: J2-TFT-DISPLAY.pin1, J2-TFT-DISPLAY.pin8, R5.Pin_0, J3-SDCARD.pin5
  N3: J2-TFT-DISPLAY.pin4, R4.Pin_0

notes:
  1) https://www.amazon.com/Connector-40p-98-Finger-Through-Durable/dp/B09MZXJ8Q3/ref=sr_1_15?crid=XJIJ1S8Y0NPS&keywords=edge%2Bconnector%2B0.1%2Binches&qid=1644340803&sprefix=edge%2Bconnector%2B0.1%2Binches%2Caps%2C406&sr=8-15&th=1
  2) https://www.amazon.com/HiLetgo-ESP-WROOM-32-Development-Microcontroller-Integrated/dp/B0718T232Z/ref=sr_1_10?keywords=ESP32+38+pin&qid=1644360022&sr=8-10
  3) https://www.amazon.com/KeeYees-Channels-Converter-Bi-Directional-Shifter/dp/B07LG646VS/ref=sr_1_3?keywords=4-channel+I2C-safe+Bi-directional+Logic+Level+Converter+-+BSS138&qid=1644509232&sr=8-3
  unused pins

custom parts:
  Adafruit 4-channel I2C-safe Bi-directional Logic Level Converter: Because the Arduino (and Basic Stamp) are 5V devices, and most modern sensors, displays, flash cards and modes are 3.3V-only, many makers find that they need to perform level shifting/conversion to protect the 3.3V device from 5V. We do have some other handy level shifters in the shop, from the DIP 74LVC245 to the fancy bi-directional TXB0108. However, neither of these are happy to work with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
  ESP32-38PinWide: Generic 38-Pin ESP32 with wide format (only access to one side of pins on a breadboard) based on Stephen Lilley's HiLetgo ESP-WROOM-32 ESP32 ESP-32S Development Board.
